# Fritzing sketch uhppoted-wiegand-pico (saved by Fritzing 0.9.10b)
breadboards: 3

parts:
  M1 = RioRand LM2596
  J1 = female pin header, 2 pins [form="♀ (female)"]
  Part1 = Adafruit 4-channel I2C-safe Bi-directional Logic Level Converter [part_number="Adafruit #757"]
  J2 = female pin header, 2 pins [form="♀ (female)"]
  LED1 = LED - 3mm [color="Orange (620nm)" current=0.030 package="3 mm [THT]"]
  LED2 = LED - 3mm [color="Green (555nm)" current=0.030 package="3 mm [THT]"]
  LED4 = LED - 3mm [color="Red (635nm)" current=0.030 package="3 mm [THT]"]
  R1 = Resistor [tolerance=±5% resistance=1k package="0402 [SMD]"]
  R2 = Resistor [tolerance=±5% resistance=1k package="0402 [SMD]"]
  R3 = Resistor [tolerance=±5% resistance=1k package="0402 [SMD]"]
  R4 = Resistor [tolerance=±5% resistance=1k package="0402 [SMD]"]
  LED3 = LED - 3mm [color="Yellow (585nm)" current=0.030 package="3 mm [THT]"]
  R5 = Resistor [tolerance=±5% resistance=1k package="0402 [SMD]"]
  J3 = Piezo Speaker
  J4 = female pin header, 2 pins [form="♀ (female)"]
  J5 = female pin header, 3 pins [form="♀ (female)"]
  Mod1 = Raspberry Pi Pico
  Part2 = Adafruit SDIO microSD Breakout

nets:
  N1: M1.Pin_1, J1.pin2
  GND: M1.Pin_2, M1.Pin_4, J1.pin1, Part1.GND, J2.pin1, LED4.cathode, R5.Pin_1, J5.pin2, Mod1.pin_3, Mod1.pin_8, Mod1.pin_10, Mod1.pin_13, Mod1.pin_18, Mod1.pin_23, Mod1.pin_28, Mod1.pin_33, Mod1.pin_38, Mod1.pin_42, Part2.GND, Part2.SCLK, Part2.CS
  N2: M1.Pin_3, J2.pin2, Mod1.pin_39
  N3: Part1.A3, Mod1.pin_26, Mod1.pin_27
  N4: Part1.A2, Mod1.pin_21, Mod1.pin_25
  N5: Part1.A1, Mod1.pin_22, Mod1.pin_24
  N6: Part1.LV, R1.Pin_0, R2.Pin_0, R3.Pin_0, R4.Pin_0, J3.pin2, Mod1.pin_36, Part2.3.3V
  N7: LED1.cathode, Mod1.pin_15
  N8: LED1.anode, R2.Pin_1
  N9: LED2.cathode, Mod1.pin_14
  N10: LED2.anode, R1.Pin_1
  N11: LED4.anode, R3.Pin_1
  N12: R4.Pin_1, LED3.anode
  N13: LED3.cathode, Mod1.pin_17
  N14: R5.Pin_0, J3.pin1
  N15: J4.pin1, Mod1.pin_2
  N16: J4.pin2, Mod1.pin_1
  N17: J5.pin1, Mod1.pin_43
  N18: J5.pin3, Mod1.pin_41
  N19: Mod1.pin_7, Part2.DO
  N20: Mod1.pin_11, Part2.DI

custom parts:
  Adafruit 4-channel I2C-safe Bi-directional Logic Level Converter: Because the Arduino (and Basic Stamp) are 5V devices, and most modern sensors, displays, flash cards and modes are 3.3V-only, many makers find that they need to perform level shifting/conversion to protect the 3.3V device from 5V. We do have some other handy level shifters in the shop, from the DIP 74LVC245 to the fancy bi-directional TXB0108. However, neither of these are happy to work with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
  Raspberry Pi Pico: Raspberry Pi Pico. Based around the RP2040 microcontroller the Pico is a low cost microcontroller device bringing Raspberry Pi quality, cost, and easy of use to the microcontroller space. Jan 2021, Split part in to two versions: tht (this one) and SMD. This one will drill holes for a .1 in header in pcb to allow plugging in the module as well as providing pads to solder the module to the top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
